# Fritzing sketch nmea_fritz_schema (saved by Fritzing 0.9.3b)
perfboards: 1

parts:
  Componente1 = Arduino Nano (Rev3.0)
  U1 = SUP500F [package=sup500f]
  R1 = Resistor [tolerance=±5% resistance=10k package="2512 [SMD]"]
  R2 = Resistor [tolerance=±5% resistance=4.7k package="2512 [SMD]"]

nets:
  N1: Componente1.GND, R1.Pin_0
  N2: Componente1.D3, R2.Pin_0
  N3: Componente1.D4, U1.TX-O
  3V3: Componente1.3V3, U1.VCC
  N4: U1.RX-I, R1.Pin_1, R2.Pin_1

notes:
  OpenWD schema
  4.7Ko
  10Ko
  TX
  RX
